# Fritzing sketch arduino_car_relay (saved by Fritzing 0.9.4)
breadboards: 1

parts:
  D1 = Rectifier Diode [part_number=1N4007 package="300 mil [THT]"]
  K1 = RELAY [part_number=80A package=relay-g5q]
  Q1 = TRANSISTOR_NPN [part_number=BC337 package=to-92]
  R2 = Resistor [tolerance=±5% resistance=470 package="2010 [SMD]"]
  R3 = Resistor [tolerance=±5% resistance=100k package="2010 [SMD]"]
  C1 = Capacitor Polarized [part_number="10µF 50V" package=panasonic_g]
  R4 = Resistor [tolerance=±5% resistance=47k package="2010 [SMD]"]
  U2 = Voltage Regulator - 5V [package="TO220 [THT]"]
  C2 = Ceramic Capacitor [capacitance="100 nF" package="0603 [SMD, multilayer]"]
  F2 = FUSE [part_number=100mA package=fuse_5mm]
  F1 = FUSE [part_number=500mA package=fuse_5mm]
  D3 = Zener Diode [part_number=1N4733A breakdown_voltage=5.1V package="300 mil [THT]"]
  R1 = Resistor [tolerance=±5% resistance=43k package="2010 [SMD]"]
  D2 = smd LED [color="Green (565nm)" package="0603 [SMD]"]
  Arduino = Arduino Pro Mini (5V) [part_number=U1]
  S2 = SWITCH-SPST-2 [part_number=on package=r_sw_th]
  S1 = SWITCH-SPST-2 [part_number=automatic package=r_sw_th]

nets:
  N1: D1.cathode, K1.COIL2, D2.anode
  N2: D1.anode, K1.COIL1, Q1.C, R1.Pin_0, S2.P
  switched 12V out: K1.MAIN
  12V from battery: K1.NO, F1.1
  ground: Q1.E, C1.-, R4.Pin_1, U2.GND, C2.0, D3.anode, Arduino.GND
  N3: Q1.B, R2.Pin_1
  N4: R2.Pin_0, Arduino.D8
  N5: R3.Pin_0, F2.2
  N6: R3.Pin_1, C1.+, R4.Pin_0, C2.1, D3.cathode, Arduino.D2
  N7: U2.input_voltage, S1.O
  N8: U2.output_voltage, Arduino.VCC
  engine running signal 0V/12V: F2.1
  N9: F1.2, S1.P
  N10: R1.Pin_1, D2.cathode
  gnd out: S2.O

custom parts:
  Arduino Pro Mini (5V): It's blue! It's thin! It's the Arduino Pro Mini! SparkFun's minimal design approach to Arduino. This is a 5V Arduino running the 16MHz bootloader. Arduino Pro Mini does not come with connectors populated so that you can solder in any connector or wire with any orientation you need. We recommend first time Arduino users start with the Uno R3. It's a great board that will get you up and running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
